// Logisim project Project2Given.circ as structural Verilog: 4 circuits, main circuit main
module main (
);

  wire and_1_out, and_2_out, B0, B1, B2, B3, B4, B5, B6, B7, B8, B9, BL, BU, C0, C1, C2, CLK, L1_l, L1_u,
       not_1_out, or_8_out, P1_v, R0, R1, R3, R4, register_3_p3, register_4_p1, register_4_p2, Valid;
  wire [2:0] counter_1_q;
  wire [3:0] IB1_c0, P1_b0, register_1_q;

  Button n1 (.out(B1));
  Button n4 (.out(B4));
  Button n7 (.out(B7));
  Button L (.out(BL));
  Button n3 (.out(B3));
  Button n2 (.out(B2));
  Button n6 (.out(B6));
  Button n5 (.out(B5));
  Button n9 (.out(B9));
  Button n8 (.out(B8));
  Button U (.out(BU));
  Button n0 (.out(B0));
  or or_1 (R0, B3, B2, B1);
  or or_2 (R1, B6, B5, B4);
  or or_3 (R3, B9, B8, B7);
  or or_4 (R4, BU, B0, BL);
  or or_5 (C0, B1, B4, B7, BL);
  or or_6 (C1, B2, B5, B8, B0);
  or or_7 (C2, B3, B6, B9, BU);
  Clock clock_1 (.out(CLK));
  nand nand_1 (Valid, IB1_c0[0], IB1_c0[1], IB1_c0[2], IB1_c0[3]);
  // Probe on P1_b0
  Panel P1 (
    .R0(R0), .R1(R1), .R2(R3), .R3(R4), .C0(C0), .C1(C1), .C2(C2), .B0(P1_b0[0]), .B1(P1_b0[1]),
    .B2(P1_b0[2]), .B3(P1_b0[3]), .V(P1_v));
  LED Press (.in(P1_v));
  // Probe on IB1_c0
  InputBuffer IB1 (
    .B0(P1_b0[0]), .B1(P1_b0[1]), .B2(P1_b0[2]), .B3(P1_b0[3]), .V(P1_v), .CLK(not_1_out), .C0(IB1_c0[0]),
    .C1(IB1_c0[1]), .C2(IB1_c0[2]), .C3(IB1_c0[3]));
  not not_1 (not_1_out, CLK);
  Register #(.width(4)) register_1 (.Q(register_1_q));  // open: D, en, clk, clr
  Lock L1 (.C0(IB1_c0[0]), .C1(IB1_c0[1]), .C2(IB1_c0[2]), .C3(IB1_c0[3]), .CLK(CLK), .L(L1_l), .U(L1_u));
  Counter #(.width(3), .max('h7)) counter_1 (
    .count(or_8_out), .Q(counter_1_q), .clk(CLK));  // open: load, D, carry, clr
  or or_8 (or_8_out, L1_l, L1_u);
  Register #(.width(4)) register_2 (.clr(register_4_p1));  // open: D, en, Q, clk
  LED Unlocked (.in(and_1_out));
  and and_1 (and_1_out, ~counter_1_q[0], ~counter_1_q[1], ~counter_1_q[2]);  // AND_Gate
  // Register #(.width(4)) register_3: pin names not known; wires that end beside it: register_1_q, register_1_q, register_3_p3, Valid
  LED Locked (.in(and_2_out));
  and and_2 (and_2_out, ~counter_1_q[0], ~counter_1_q[1], counter_1_q[2]);  // AND_Gate
  // Register #(.width(4)) register_4: pin names not known; wires that end beside it: register_4_p1, register_4_p2, Valid
  // Register #(.width(4)) register_5: pin names not known; wires that end beside it: register_3_p3, register_3_p3, IB1_c0, Valid
endmodule

module Panel (
  input  R0,
  input  R1,
  input  R2,
  input  R3,
  input  C0,
  input  C1,
  input  C2,
  output B0,
  output B1,
  output B2,
  output B3,
  output V
);

  wire and_1_out, and_2_out, and_3_out, and_4_out, and_5_out, and_6_out, and_7_out, and_8_out, and_9_out,
       and_10_out, and_12_out, and_13_out, and_14_out, and_15_out, and_16_out, and_17_out, and_18_out,
       and_19_out, CisEven, CisValid, nor_1_out, nor_2_out, nor_3_out, nor_4_out, nor_5_out, nor_6_out,
       nor_7_out, not_1_out, not_2_out, or_1_out, or_5_out, RisValid;

  nor nor_1 (nor_1_out, C1, C2);
  nor nor_2 (nor_2_out, C0, C2);
  nor nor_3 (nor_3_out, C1, C0);
  and and_1 (and_1_out, C0, nor_1_out);
  and and_2 (and_2_out, C1, nor_2_out);
  and and_3 (and_3_out, C2, nor_3_out);
  and and_4 (and_4_out, CisEven, or_1_out);
  or or_1 (or_1_out, R0, R2);
  and and_5 (and_5_out, R1, C1);
  and and_6 (and_6_out, C2, R3);
  or or_2 (CisValid, and_1_out, and_2_out, and_3_out);
  or or_3 (B3, and_4_out, and_5_out, and_6_out);
  and and_7 (and_7_out, R0, nor_4_out);
  nor nor_4 (nor_4_out, R1, R2, R3);
  and and_8 (and_8_out, R1, nor_5_out);
  nor nor_5 (nor_5_out, R0, R2, R3);
  and and_9 (and_9_out, R2, nor_6_out);
  nor nor_6 (nor_6_out, R1, R0, R3);
  and and_10 (and_10_out, R3, nor_7_out);
  nor nor_7 (nor_7_out, R1, R2, R0);
  and and_11 (V, RisValid, CisValid);
  or or_4 (RisValid, and_7_out, and_8_out, and_9_out, and_10_out);
  or or_5 (or_5_out, C1, C2);
  not not_1 (not_1_out, C1);
  not not_2 (not_2_out, C1);
  and and_12 (and_12_out, R0, or_5_out);
  and and_13 (and_13_out, R1, C2);
  and and_14 (and_14_out, R2, C0);
  and and_15 (and_15_out, R3, not_1_out);
  and and_16 (and_16_out, R3, not_2_out);
  and and_17 (and_17_out, R2, C1);
  and and_18 (and_18_out, R2, C2);
  or or_6 (B1, R1, and_19_out);
  and and_19 (and_19_out, R2, C0);
  or or_7 (B0, and_16_out, and_17_out, and_18_out);
  or or_8 (B2, and_12_out, and_13_out, and_14_out, and_15_out);
  or or_9 (CisEven, C0, C2);
endmodule

module InputBuffer (
  input  B0,
  input  B1,
  input  B2,
  input  B3,
  input  V,
  input  CLK,
  output C0,
  output C1,
  output C2,
  output C3
);

  wire and_1_out, and_2_out, and_3_out, and_4_out, d_ff_1_q, d_ff_1_qn, d_ff_2_q, d_ff_2_qn, not_1_out,
       not_2_out, not_3_out, not_4_out, or_1_out, SetNumber;

  and and_1 (and_1_out, d_ff_1_q, V);
  and and_2 (and_2_out, V, d_ff_2_q);
  buf and_3 (and_3_out, and_4_out);  // AND_Gate
  D_Flip_Flop d_ff_1 (.clk(CLK), .D(or_1_out), .Q(d_ff_1_q), .Qn(d_ff_1_qn));  // open: preset, en, reset
  or or_1 (or_1_out, and_1_out, and_2_out);
  D_Flip_Flop d_ff_2 (.clk(CLK), .D(and_3_out), .Q(d_ff_2_q), .Qn(d_ff_2_qn));  // open: preset, en, reset
  and and_4 (and_4_out, d_ff_1_qn, d_ff_2_qn);
  and and_5 (SetNumber, V, and_3_out);
  not not_1 (not_1_out, SetNumber);
  or or_2 (C0, not_1_out, B0);
  not not_2 (not_2_out, SetNumber);
  or or_3 (C1, not_2_out, B1);
  not not_3 (not_3_out, SetNumber);
  not not_4 (not_4_out, SetNumber);
  or or_4 (C2, not_3_out, B2);
  or or_5 (C3, not_4_out, B3);
endmodule

module Lock (
  input  C0,
  input  C1,
  input  C2,
  input  C3,
  input  CLK,
  output L,
  output U
);
endmodule
